// Logisim project datapath.circ as structural Verilog
module DataPath (
);

  wire [15:0] PC_q, ProgramROM_data, undriven;

  Register #(.width(16)) PC (.D(undriven), .Q(PC_q));  // open: en, clk, clr
  ROM #(.addrWidth(16), .dataWidth(16)) ProgramROM (.addr(PC_q), .data(ProgramROM_data));
  Register #(.width(16)) InstructionRegister (.D(ProgramROM_data));  // open: en, clk, Q, clr
  RegisterFile registerfile_1 ();  // open: i_Clk, i_Rst, i_SelX, i_SelY, i_WriteEnable, i_WriteData, o_DataX, o_DataY
  Register ResultRegister ();  // open: D, en, clk, Q, clr
endmodule

// VHDL entity RegisterFile, as the project stores it:
library ieee;
use ieee.std_logic_1164.all;
use ieee.numeric_std_unsigned.all;

entity RegisterFile is
    port (
        i_Clk : in std_logic;
        i_Rst : in std_logic;
        i_SelX : in std_logic_vector(3 downto 0);
        i_SelY : in std_logic_vector(3 downto 0);
        i_WriteEnable : in std_logic;
        i_WriteData : in std_logic_vector(7 downto 0);
        o_DataX : out std_logic_vector(7 downto 0);
        o_DataY : out std_logic_vector(7 downto 0)
    );
end RegisterFile;

architecture RTL of RegisterFile is

    signal r_Registers: reg_arr_t;

begin

    process(i_Clk, i_Rst) is
    begin
        if rising_edge(i_Clk) then
            if i_Rst = '1' then
                r_Registers <= (others => (others => '0'));
            elsif i_WriteEnable = '1'
                then r_Registers(to_integer(i_SelX)) <= i_WriteData;
            end if;
        end if;
    end process;

    o_DataX <= r_Registers(to_integer(i_SelX));
    o_DataY <= r_Registers(to_integer(i_SelY));

end architecture;
